# Fritzing sketch morse (saved by Fritzing 0.9.3b)
breadboards: 1

parts:
  Transmitter = Arduino Uno (Rev3)
  Receiver = Arduino Uno (Rev3)
  J1 = Piezo Speaker
  R1 = Resistor [tolerance=±5% resistance=100 package=THT]

nets (from the breadboard view):
  N1: Transmitter.D9_PWM, Receiver.D9_PWM, R1.Pin_1
  GND: Transmitter.GND, Receiver.GND, J1.pin1
  N2: J1.pin2, R1.Pin_0
